# Fritzing sketch Vario (saved by Fritzing 0.9.3b)
perfboards: 1

parts:
  Bauteil1 = Arduino Uno (Rev3)
  Bauteil2 = Barometric Pressure Sensor - BMP180 Breakout (GY-68)
  U1 = LCD-16X2 [package=lcd-16x2]
  R1 = Resistor [tolerance=±5% resistance=220 package=THT]
  R2 = Resistor [tolerance=±5% resistance=220 package=THT]
  S1 = Taiway 100-SP-X-T1 SPDT Miniature Toggle Switch [part_number=100-SP-X-T1-0-0-B1-M1 package=THT]
  S2 = Taiway 100-SP-X-T1 SPDT Miniature Toggle Switch [part_number=100-SP-X-T1-0-0-B1-M1 package=THT]
  S3 = Taiway 100-SP-X-T1 SPDT Miniature Toggle Switch [part_number=100-SP-X-T1-0-0-B1-M1 package=THT]
  S4 = Taiway 100-SP-X-T1 SPDT Miniature Toggle Switch [part_number=100-SP-X-T1-0-0-B1-M1 package=THT]
  J1 = Piezo Speaker

nets:
  N1: Bauteil1.A4/SDA, Bauteil2.SDA
  N2: Bauteil1.A5/SCL, Bauteil2.SCL
  N3: Bauteil1.D8, S2.COM
  N4: Bauteil1.D9_PWM, S1.COM
  N5: Bauteil1.D10_PWM/SS, S3.COM
  N6: Bauteil1.D11_PWM/MOSI, U1.E
  N7: Bauteil1.D12/MISO, U1.RS
  N8: Bauteil1.D2, U1.DB7
  N9: Bauteil1.D3_PWM, U1.DB6
  N10: Bauteil1.D4, U1.DB5
  N11: Bauteil1.D5_PWM, U1.DB4
  N12: Bauteil1.D6_PWM, J1.pin2
  N13: Bauteil1.D7, S4.COM
  3V3: Bauteil1.3V3, Bauteil2.VCC
  N14: U1.VO, R1.Pin_0
  N15: U1.A, R2.Pin_0

notes:
  220 Ohm
  max Range Flighttime
  height m/ft
  vario
  Sound
